// Digital circuit AS6C4008.dig as structural Verilog
// 512K X 8 BIT CMOS SRAM
module AS6C4008 (
  input  A0,
  input  A1,
  input  A2,
  input  A3,
  input  A4,
  input  A5,
  input  A6,
  input  A7,
  input  A8,
  input  A9,
  input  A10,
  input  A11,
  input  A12,
  input  nCE,
  input  nOE,
  input  nWE,
  input  VCC,
  input  GND,
  input  A13,
  input  A14,
  input  A15,
  input  A16,
  input  A17,
  input  A18,
  output DQ0,
  output DQ1,
  output DQ2,
  output DQ3,
  output DQ4,
  output DQ5,
  output DQ6,
  output DQ7
);

  wire nor_1_out;
  wire [7:0] RAM_d;

  PowerSupply powersupply_1 (.VDD(VCC), .GND(GND));
  RAMSinglePortSel #(.AddrBits(19), .isProgramMemory("true"), .Bits(8)) RAM (
    .A({A18, A17, A16, A15, A14, A13, A12, A11, A10, A9, A8, A7, A6, A5, A4, A3, A2, A1, A0}), .CS(~nCE),
    .WE(~nWE), .OE(~nOE), .D(RAM_d));
  nor nor_1 (nor_1_out, nCE, ~nWE, nOE);  // NOr
  BusSplitter #(.Bits(8)) bussplitter_1 (
    .D(RAM_d), .OE(nor_1_out), .D0(DQ0), .D1(DQ1), .D2(DQ2), .D3(DQ3), .D4(DQ4), .D5(DQ5), .D6(DQ6), .D7(DQ7));

  // Notes on the sheet:
  //   A0: pin 12
  //   A1: pin 11
  //   A2: pin 10
  //   A3: pin 9
  //   A4: pin 8
  //   A5: pin 7
  //   A6: pin 6
  //   A7: pin 5
  //   A8: pin 27
  //   A9: pin 26
  //   A10: pin 23
  //   A11: pin 25
  //   A12: pin 4
  //   nCE: pin 22, default 1
  //   nOE: pin 24, default 1
  //   nWE: pin 29, default 1
  //   DQ0: pin 13
  //   DQ1: pin 14
  //   DQ2: pin 15
  //   DQ3: pin 17
  //   DQ4: pin 18
  //   DQ5: pin 19
  //   DQ6: pin 20
  //   DQ7: pin 21
  //   VCC: pin 32, default 1
  //   GND: pin 16
  //   A13: pin 28
  //   A14: pin 3
  //   A15: pin 31
  //   A16: pin 2
  //   A17: pin 30
  //   A18: pin 1
endmodule
