// Digital circuit K16 CPU.dig as structural Verilog
module K16_CPU (
  input  Clock,
  input  nIRQ0,
  input  nIRQ1,
  input  nIRQ2,
  input  nIRQ3,
  input  nIRQ4,
  input  nIRQ5,
  input  nIRQ6,
  input  nIRQ7,
  input  INT_Timer_6Hz
);

  wire _74138_1_pin1, _74138_1_pin2, _74138_1_pin3, _74138_2_pin1, _74138_2_pin2, _74138_2_pin3, A0, A1, A2,
       A3, A4, A5, A6, A7, A8, A9, A10, A11, A12, A13, A14, A15, A16, A17, A18, A19, A20, A21, A22, A23,
       AAWrite0, AAWrite1, AB_Writer_pin13, AB_Writer_pin14, ABWrite0, ABWrite1, ADD0_pin9, ADD1_pin7,
       ADD1_pin9, ADD2_pin7, ADD2_pin9, ADD3_pin7, ALU_A_Writer_pin13, ALU_A_Writer_pin14, ALUA0, ALUA1,
       ALUA2, ALUA3, ALUA4, ALUA5, ALUA6, ALUA7, ALUA8, ALUA9, ALUA10, ALUA11, ALUA12, ALUA13, ALUA14,
       ALUA15, ALUB0, ALUB1, ALUB2, ALUB3, ALUB4, ALUB5, ALUB6, ALUB7, ALUB8, ALUB9, ALUB10, ALUB11, ALUB12,
       ALUB13, ALUB14, ALUB15, and_1_out, and_5_out, and_8_out, and_12_out, and_13_out, and_15_out,
       and_16_out, and_17_out, and_20_out, and_21_out, and_24_out, and_25_out, and_27_out, CarryEnable,
       CarryIn, CarryMode0, CarryMode1, CarryResult, ConditionEnable, ConditionResult, D0, D1, D2, D3, D4,
       D5, D6, D7, D8, D9, D10, D11, D12, D13, D14, D15, DB0, DB1, DB2, DB3, DB4, DB5, DB6, DB7, DB8, DB9,
       DB10, DB11, DB12, DB13, DB14, DB15, DBRead0, DBRead1, EnablePCClk, F0, F1, F2, F3, FlagCARRY, FlagNEG,
       FlagOVERFLOW, FLAGS_MUX_pin14, FLAGSLoad, FLAGSX, FlagZERO, HaltCPU, INT0, INT1, INT2, INT_Ack,
       INT_Ack__IR_Disable_pin13, INTClear, INTCondition, INTEnable, INTEnabled, INTLoad, IR0, IR1, IR2, IR3,
       IR4, IR5, IR6, IR7, IR8, IR9, IR10, IR11, IR12, IR13, IR14, IR15, IR_Disable, MemAccess, nAAWrite00xx,
       nAAWriteDR, nAAWriteFFxx, nAAWriteT16, nABWriteLOA, nABWritePOA, nABWriterORAB, nABWriterORABY,
       nABWriterPC, nABWriterXY, nABWriteTOA, nABWriteZOA, nand_1_out, nand_2_out, nand_3_out, nand_4_out,
       nand_6_out, nand_7_out, nBranchTaken, nClk, nDBReadDR, nDBReadFLAGS, nDBReadIR, nDBReadMemByte,
       nDBReadMemWord, nDBReadNOTHING, nDBReadPC, nDBReadT8, nDBReadT16, nDBReadTEMP, nDBReadX, nDBReadY,
       nDBRWMemByte, nDBWriteAB_HI, nDBWriteAB_LO, nDBWriteFLAGS, nDBWriteMemByte, nDBWriteMemWord,
       nDBWriteNOTHING, nDBWriteORDB, nDBWriteT8, nFlagCARRY, nFLAGSX, nINT_Ack, nINTEnabled, nIR_Disable,
       nIRQ, nMEM_20, nMEM_30, nMEM_40, nMEM_50, nMEM_60, nMEM_70, nMEM_80, nMEM_90, nMEM_A0, nMEM_B0,
       nMEM_C0, nMEM_D0, nMEM_D80000, nMEM_D90000, nMEM_DA0000, nMEM_DB0000, nMEM_DC0000, nMEM_DD0000,
       nMEM_DE0000, nMEM_DF0000, nOE_HIGH, nOE_LOW, nOEHighHigh, nOEHighLow, nOELowLow, nor_2_out, nor_3_out,
       not_3_out, not_4_out, not_5_out, not_6_out, not_9_out, not_10_out, not_11_out, not_12_out, not_13_out,
       not_14_out, not_15_out, not_17_out, not_18_out, not_19_out, nRAM_00_CS, nRAM_10_CS, nReset,
       nRESET_out, nROM_E0_CS, nROM_F0_CS, nuReset, nWE_HIGH, nWE_LOW, or_1_out, or_2_out, or_3_out,
       or_5_out, or_9_out, or_10_out, or_11_out, or_12_out, or_13_out, ORABLoad, ORDBLoad, PC1, PC1_pin10,
       PC1_pin15, PC2, PC2_pin15, PC3, PC3_pin15, PC4, PC4_pin9, PC4_pin15, PC5, PC6, PC7, PC8, PC9, PC10,
       PC11, PC12, PC13, PC14, PC15, PC16, PC17, PC18, PC19, PC20, PC21, PC22, PC23, PCEnable, pullup_9_out,
       pullup_26_out, R_nW, Reset, RESULT0, RESULT1, RESULT2, RESULT3, RESULT4, RESULT5, RESULT6, RESULT7,
       RESULT8, RESULT9, RESULT10, RESULT11, RESULT12, RESULT13, RESULT14, RESULT15, SccTrue, seq0, seq1,
       seq2, seq3, T0, T1, T2, T3, T4, T5, T6, T7, T8_TEMP_REGISTER_pin11, uReset, xor_1_out, xor_2_out,
       xor_3_out, xor_4_out, Y0_REGISTER_pin11, ZeroFlag0, ZeroFlag1, ZeroFlag2, ZeroFlag3;
  wire [15:0] _74541_1_pin2;

  and and_1 (and_1_out, nDBReadPC, nBranchTaken);
  and and_2 (EnablePCClk, nClk, PCEnable);
  or or_1 (or_1_out, nDBReadPC, DBRead0);
  PullUp pullup_1 (.out(T1));
  PullUp pullup_2 (.out(T0));
  PullUp pullup_3 (.out(T5));
  PullUp pullup_4 (.out(T4));
  Seven_Seg_Hex seven_seg_hex_1 (.d({PC23, PC22, PC21, PC20}), .dp(1'b0));
  PullUp pullup_5 (.out(T3));
  PullUp pullup_6 (.out(T2));
  PullUp pullup_7 (.out(T7));
  PullUp pullup_8 (.out(T6));
  Seven_Seg_Hex seven_seg_hex_2 (.d({PC19, PC18, PC17, PC16}), .dp(1'b0));
  Reset u_nRESET (.out(nRESET_out));
  Seven_Seg_Hex seven_seg_hex_3 (.d({PC15, PC14, PC13, PC12}), .dp(1'b0));
  _74161 PC0 (
    .pin1(nReset), .pin2(Clock), .pin3(D1), .pin4(D2), .pin5(D3), .pin6(1'b0), .pin7(EnablePCClk),
    .pin8(1'b0), .pin9(and_1_out), .pin10(EnablePCClk), .pin12(PC3), .pin13(PC2), .pin14(PC1), .pin16(1'b1));  // open: pin11, pin15
  _74161 u_PC1 (
    .pin1(nReset), .pin2(Clock), .pin3(D4), .pin4(D5), .pin5(D6), .pin6(D7), .pin7(EnablePCClk), .pin8(1'b0),
    .pin9(and_1_out), .pin10(PC1_pin10), .pin11(PC7), .pin12(PC6), .pin13(PC5), .pin14(PC4),
    .pin15(PC1_pin15), .pin16(1'b1));
  _74161 u_PC2 (
    .pin1(nReset), .pin2(Clock), .pin3(D8), .pin4(D9), .pin5(D10), .pin6(D11), .pin7(EnablePCClk),
    .pin8(1'b0), .pin9(and_1_out), .pin10(PC1_pin15), .pin11(PC11), .pin12(PC10), .pin13(PC9), .pin14(PC8),
    .pin15(PC2_pin15), .pin16(1'b1));
  _74161 u_PC3 (
    .pin1(nReset), .pin2(Clock), .pin3(D12), .pin4(D13), .pin5(D14), .pin6(D15), .pin7(EnablePCClk),
    .pin8(1'b0), .pin9(and_1_out), .pin10(PC2_pin15), .pin11(PC15), .pin12(PC14), .pin13(PC13), .pin14(PC12),
    .pin15(PC3_pin15), .pin16(1'b1));
  PullUp pullup_9 (.out(pullup_9_out));
  _74161 u_PC4 (
    .pin1(pullup_9_out), .pin2(Clock), .pin3(T0), .pin4(T1), .pin5(T2), .pin6(T3), .pin7(EnablePCClk),
    .pin8(1'b0), .pin9(PC4_pin9), .pin10(PC3_pin15), .pin11(PC19), .pin12(PC18), .pin13(PC17), .pin14(PC16),
    .pin15(PC4_pin15), .pin16(1'b1));
  _74161 u_PC5 (
    .pin1(pullup_9_out), .pin2(Clock), .pin3(T4), .pin4(T5), .pin5(T6), .pin6(T7), .pin7(EnablePCClk),
    .pin8(1'b0), .pin9(PC4_pin9), .pin10(PC4_pin15), .pin11(PC23), .pin12(PC22), .pin13(PC21), .pin14(PC20),
    .pin16(1'b1));  // open: pin15
  _74161 Reset_Delay__DIgital_Issue (
    .pin1(nRESET_out), .pin2(Clock), .pin3(1'b0), .pin4(1'b0), .pin5(1'b0), .pin6(1'b0), .pin7(1'b1),
    .pin8(1'b0), .pin9(1'b1), .pin10(Reset), .pin12(nReset), .pin16(1'b1));  // open: pin11, pin13, pin14, pin15
  Seven_Seg_Hex seven_seg_hex_4 (.d({PC11, PC10, PC9, PC8}), .dp(1'b0));
  and and_3 (PC4_pin9, nReset, or_1_out);
  not not_1 (nClk, Clock);
  Seven_Seg_Hex seven_seg_hex_5 (.d({PC7, PC6, PC5, PC4}), .dp(1'b0));
  not not_2 (Reset, nReset);
  Seven_Seg_Hex seven_seg_hex_6 (.d({PC3, PC2, PC1, 1'b0}), .dp(1'b0));
  and and_4 (PC1_pin10, PC1, PC2, PC3, nClk);
  Seven_Seg_Hex seven_seg_hex_7 (.d({A23, A22, A21, A20}), .dp(1'b0));
  Seven_Seg_Hex seven_seg_hex_8 (.d({A19, A18, A17, A16}), .dp(1'b0));
  _74541 AB_DB_0 (
    .pin1(nDBWriteAB_LO), .pin2(A0), .pin3(A1), .pin4(A2), .pin5(A3), .pin6(A4), .pin7(A5), .pin8(A6),
    .pin9(A7), .pin10(1'b0), .pin11(D7), .pin12(D6), .pin13(D5), .pin14(D4), .pin15(D3), .pin16(D2),
    .pin17(D1), .pin18(D0), .pin19(nDBWriteAB_LO), .pin20(1'b1));
  _74541 AB_DB_1 (
    .pin1(nDBWriteAB_LO), .pin2(A8), .pin3(A9), .pin4(A10), .pin5(A11), .pin6(A12), .pin7(A13), .pin8(A14),
    .pin9(A15), .pin10(1'b0), .pin11(D15), .pin12(D14), .pin13(D13), .pin14(D12), .pin15(D11), .pin16(D10),
    .pin17(D9), .pin18(D8), .pin19(nDBWriteAB_LO), .pin20(1'b1));
  _74541 AB_DB_HI (
    .pin1(nDBWriteAB_HI), .pin2(A16), .pin3(A17), .pin4(A18), .pin5(A19), .pin6(A20), .pin7(A21), .pin8(A22),
    .pin9(A23), .pin10(1'b0), .pin11(D7), .pin12(D6), .pin13(D5), .pin14(D4), .pin15(D3), .pin16(D2),
    .pin17(D1), .pin18(D0), .pin19(nDBWriteAB_HI), .pin20(1'b1));
  _74541 PC_AB_0 (
    .pin1(nABWriterPC), .pin2(1'b0), .pin3(PC1), .pin4(PC2), .pin5(PC3), .pin6(PC4), .pin7(PC5), .pin8(PC6),
    .pin9(PC7), .pin10(1'b0), .pin11(A7), .pin12(A6), .pin13(A5), .pin14(A4), .pin15(A3), .pin16(A2),
    .pin17(A1), .pin18(A0), .pin19(nABWriterPC), .pin20(1'b1));
  _74541 PC_AB_1 (
    .pin1(nABWriterPC), .pin2(PC8), .pin3(PC9), .pin4(PC10), .pin5(PC11), .pin6(PC12), .pin7(PC13),
    .pin8(PC14), .pin9(PC15), .pin10(1'b0), .pin11(A15), .pin12(A14), .pin13(A13), .pin14(A12), .pin15(A11),
    .pin16(A10), .pin17(A9), .pin18(A8), .pin19(nABWriterPC), .pin20(1'b1));
  and and_5 (and_5_out, nABWriterPC, nABWritePOA);
  _74541 PC_AB_HI (
    .pin1(and_5_out), .pin2(PC16), .pin3(PC17), .pin4(PC18), .pin5(PC19), .pin6(PC20), .pin7(PC21),
    .pin8(PC22), .pin9(PC23), .pin10(1'b0), .pin11(A23), .pin12(A22), .pin13(A21), .pin14(A20), .pin15(A19),
    .pin16(A18), .pin17(A17), .pin18(A16), .pin19(and_5_out), .pin20(1'b1));
  Seven_Seg_Hex seven_seg_hex_9 (.d({A15, A14, A13, A12}), .dp(1'b0));
  Seven_Seg_Hex seven_seg_hex_10 (.d({A11, A10, A9, A8}), .dp(1'b0));
  Seven_Seg_Hex seven_seg_hex_11 (.d({A7, A6, A5, A4}), .dp(1'b0));
  Seven_Seg_Hex seven_seg_hex_12 (.d({A3, A2, A1, A0}), .dp(1'b0));
  _74670 X0_REGISTER (
    .pin1(D1), .pin2(D2), .pin3(D3), .pin4(ABWrite1), .pin5(ABWrite0), .pin6(A3), .pin7(A2), .pin8(1'b0),
    .pin9(A1), .pin10(A0), .pin11(nABWriterXY), .pin12(nDBReadX), .pin13(DBRead1), .pin14(DBRead0),
    .pin15(D0), .pin16(1'b1));
  _74670 X1_REGISTER (
    .pin1(D5), .pin2(D6), .pin3(D7), .pin4(ABWrite1), .pin5(ABWrite0), .pin6(A7), .pin7(A6), .pin8(1'b0),
    .pin9(A5), .pin10(A4), .pin11(nABWriterXY), .pin12(nDBReadX), .pin13(DBRead1), .pin14(DBRead0),
    .pin15(D4), .pin16(1'b1));
  _74670 X2_REGISTER (
    .pin1(D9), .pin2(D10), .pin3(D11), .pin4(ABWrite1), .pin5(ABWrite0), .pin6(A11), .pin7(A10), .pin8(1'b0),
    .pin9(A9), .pin10(A8), .pin11(nABWriterXY), .pin12(nDBReadX), .pin13(DBRead1), .pin14(DBRead0),
    .pin15(D8), .pin16(1'b1));
  _74670 X3_REGISTER (
    .pin1(D13), .pin2(D14), .pin3(D15), .pin4(ABWrite1), .pin5(ABWrite0), .pin6(A15), .pin7(A14),
    .pin8(1'b0), .pin9(A13), .pin10(A12), .pin11(nABWriterXY), .pin12(nDBReadX), .pin13(DBRead1),
    .pin14(DBRead0), .pin15(D12), .pin16(1'b1));
  _74670 Y0_REGISTER (
    .pin1(D1), .pin2(D2), .pin3(D3), .pin4(ABWrite1), .pin5(ABWrite0), .pin6(A19), .pin7(A18), .pin8(1'b0),
    .pin9(A17), .pin10(A16), .pin11(Y0_REGISTER_pin11), .pin12(nDBReadY), .pin13(DBRead1), .pin14(DBRead0),
    .pin15(D0), .pin16(1'b1));
  _74670 Y1_REGISTER (
    .pin1(D5), .pin2(D6), .pin3(D7), .pin4(ABWrite1), .pin5(ABWrite0), .pin6(A23), .pin7(A22), .pin8(1'b0),
    .pin9(A21), .pin10(A20), .pin11(Y0_REGISTER_pin11), .pin12(nDBReadY), .pin13(DBRead1), .pin14(DBRead0),
    .pin15(D4), .pin16(1'b1));
  and and_6 (Y0_REGISTER_pin11, nABWriterXY, nABWriterORABY);
  or or_2 (or_2_out, nAAWriteT16, SccTrue);
  Seven_Seg_Hex seven_seg_hex_13 (.d({D15, D14, D13, D12}), .dp(1'b0));
  Seven_Seg_Hex seven_seg_hex_14 (.d({D11, D10, D9, D8}), .dp(1'b0));
  _74574 T16W_LO (
    .pin1(or_2_out), .pin2(D0), .pin3(D1), .pin4(D2), .pin5(D3), .pin6(D4), .pin7(D5), .pin8(D6), .pin9(D7),
    .pin10(1'b0), .pin11(nDBReadT16), .pin12(ALUA7), .pin13(ALUA6), .pin14(ALUA5), .pin15(ALUA4),
    .pin16(ALUA3), .pin17(ALUA2), .pin18(ALUA1), .pin19(ALUA0), .pin20(1'b1));
  _74574 T16W_HI (
    .pin1(or_2_out), .pin2(D8), .pin3(D9), .pin4(D10), .pin5(D11), .pin6(D12), .pin7(D13), .pin8(D14),
    .pin9(D15), .pin10(1'b0), .pin11(nDBReadT16), .pin12(ALUA15), .pin13(ALUA14), .pin14(ALUA13),
    .pin15(ALUA12), .pin16(ALUA11), .pin17(ALUA10), .pin18(ALUA9), .pin19(ALUA8), .pin20(1'b1));
  _74574 T8_TEMP_REGISTER (
    .pin1(Reset), .pin2(D0), .pin3(D1), .pin4(D2), .pin5(D3), .pin6(D4), .pin7(D5), .pin8(D6), .pin9(D7),
    .pin10(1'b0), .pin11(T8_TEMP_REGISTER_pin11), .pin12(T7), .pin13(T6), .pin14(T5), .pin15(T4), .pin16(T3),
    .pin17(T2), .pin18(T1), .pin19(T0), .pin20(1'b1));
  _74541 T8_5__gt__ALUA_LO (
    .pin1(AAWrite0), .pin2(T0), .pin3(T1), .pin4(T2), .pin5(T3), .pin6(T4), .pin7(1'b0), .pin8(1'b0),
    .pin9(1'b0), .pin10(1'b0), .pin11(ALUA7), .pin12(ALUA6), .pin13(ALUA5), .pin14(ALUA4), .pin15(ALUA3),
    .pin16(ALUA2), .pin17(ALUA1), .pin18(ALUA0), .pin19(nAAWrite00xx), .pin20(1'b1));
  _74541 T8__gt__DB_LO (
    .pin1(nDBWriteT8), .pin2(T0), .pin3(T1), .pin4(T2), .pin5(T3), .pin6(T4), .pin7(1'b0), .pin8(1'b0),
    .pin9(1'b0), .pin10(1'b0), .pin11(D7), .pin12(D6), .pin13(D5), .pin14(D4), .pin15(D3), .pin16(D2),
    .pin17(D1), .pin18(D0), .pin19(nDBWriteT8), .pin20(1'b1));
  _74541 T8__gt__AB_HI (
    .pin1(nABWriteTOA), .pin2(T0), .pin3(T1), .pin4(T2), .pin5(T3), .pin6(T4), .pin7(T5), .pin8(T6),
    .pin9(T7), .pin10(1'b0), .pin11(A23), .pin12(A22), .pin13(A21), .pin14(A20), .pin15(A19), .pin16(A18),
    .pin17(A17), .pin18(A16), .pin19(nABWriterORAB), .pin20(1'b1));
  and and_7 (T8_TEMP_REGISTER_pin11, nDBReadIR, nDBReadT8);
  Seven_Seg_Hex seven_seg_hex_15 (.d({D7, D6, D5, D4}), .dp(1'b0));
  Seven_Seg_Hex seven_seg_hex_16 (.d({D3, D2, D1, D0}), .dp(1'b0));
  and and_8 (and_8_out, nDBWriteT8, nDBWriteFLAGS, nDBWriteAB_HI, nDBWriteMemByte);
  Seven_Seg_Hex seven_seg_hex_17 (.d({IR15, IR14, IR13, IR12}), .dp(1'b0));
  not not_3 (not_3_out, HaltCPU);
  Seven_Seg_Hex seven_seg_hex_18 (.d({IR11, IR10, IR9, IR8}), .dp(1'b0));
  not not_4 (not_4_out, AAWrite0);
  Seven_Seg_Hex seven_seg_hex_19 (.d({IR7, IR6, IR5, IR4}), .dp(1'b0));
  _74574 IR_LOW (
    .pin1(IR_Disable), .pin2(D0), .pin3(D1), .pin4(D2), .pin5(D3), .pin6(D4), .pin7(D5), .pin8(D6),
    .pin9(D7), .pin10(1'b0), .pin11(nDBReadIR), .pin12(IR7), .pin13(IR6), .pin14(IR5), .pin15(IR4),
    .pin16(IR3), .pin17(IR2), .pin18(IR1), .pin19(IR0), .pin20(1'b1));
  _74574 IR_HI (
    .pin1(IR_Disable), .pin2(D8), .pin3(D9), .pin4(D10), .pin5(D11), .pin6(D12), .pin7(D13), .pin8(D14),
    .pin9(D15), .pin10(1'b0), .pin11(nDBReadIR), .pin12(IR15), .pin13(IR14), .pin14(IR13), .pin15(IR12),
    .pin16(IR11), .pin17(IR10), .pin18(IR9), .pin19(IR8), .pin20(1'b1));
  _74161 Microcode_Sequencer (
    .pin1(nReset), .pin2(Clock), .pin3(1'b0), .pin4(1'b0), .pin5(1'b0), .pin6(1'b0), .pin7(not_3_out),
    .pin8(1'b0), .pin9(nuReset), .pin10(1'b1), .pin11(seq3), .pin12(seq2), .pin13(seq1), .pin14(seq0),
    .pin16(1'b1));  // open: pin15
  _74541 _02__gt__ALUA_LO__INC (
    .pin1(not_4_out), .pin2(1'b0), .pin3(AAWrite1), .pin4(1'b0), .pin5(1'b0), .pin6(1'b0), .pin7(1'b0),
    .pin8(1'b0), .pin9(1'b0), .pin10(1'b0), .pin11(ALUA7), .pin12(ALUA6), .pin13(ALUA5), .pin14(ALUA4),
    .pin15(ALUA3), .pin16(ALUA2), .pin17(ALUA1), .pin18(ALUA0), .pin19(nAAWrite00xx), .pin20(1'b1));
  _74541 _00__gt__DB_HI (
    .pin1(and_8_out), .pin2(1'b0), .pin3(1'b0), .pin4(1'b0), .pin5(1'b0), .pin6(1'b0), .pin7(1'b0),
    .pin8(1'b0), .pin9(1'b0), .pin10(1'b0), .pin11(D15), .pin12(D14), .pin13(D13), .pin14(D12), .pin15(D11),
    .pin16(D10), .pin17(D9), .pin18(D8), .pin19(and_8_out), .pin20(1'b1));
  _74541 T8__gt__AB_HI_2 (
    .pin1(nABWriteLOA), .pin2(FlagCARRY), .pin3(T1), .pin4(T2), .pin5(T3), .pin6(T4), .pin7(T5), .pin8(T6),
    .pin9(T7), .pin10(1'b0), .pin11(A23), .pin12(A22), .pin13(A21), .pin14(A20), .pin15(A19), .pin16(A18),
    .pin17(A17), .pin18(A16), .pin19(nABWriterORAB), .pin20(1'b1));
  Seven_Seg_Hex seven_seg_hex_20 (.d({IR3, IR2, IR1, IR0}), .dp(1'b0));
  PullUp pullup_10 (.out(IR0));
  PullUp pullup_11 (.out(IR1));
  PullUp pullup_12 (.out(IR8));
  PullUp pullup_13 (.out(IR9));
  PullUp pullup_14 (.out(IR2));
  PullUp pullup_15 (.out(IR3));
  PullUp pullup_16 (.out(IR10));
  PullUp pullup_17 (.out(IR11));
  PullUp pullup_18 (.out(IR4));
  PullUp pullup_19 (.out(IR5));
  PullUp pullup_20 (.out(IR12));
  PullUp pullup_21 (.out(IR13));
  PullUp pullup_22 (.out(IR6));
  PullUp pullup_23 (.out(IR7));
  PullUp pullup_24 (.out(IR14));
  PullUp pullup_25 (.out(IR15));
  not not_5 (not_5_out, AAWrite0);
  PullUp pullup_26 (.out(pullup_26_out));
  _74670 DATA0 (
    .pin1(D1), .pin2(D2), .pin3(D3), .pin4(AAWrite1), .pin5(AAWrite0), .pin6(ALUA3), .pin7(ALUA2),
    .pin8(1'b0), .pin9(ALUA1), .pin10(ALUA0), .pin11(nAAWriteDR), .pin12(nDBReadDR), .pin13(DBRead1),
    .pin14(DBRead0), .pin15(D0), .pin16(1'b1));
  _74670 DATA1 (
    .pin1(D5), .pin2(D6), .pin3(D7), .pin4(AAWrite1), .pin5(AAWrite0), .pin6(ALUA7), .pin7(ALUA6),
    .pin8(1'b0), .pin9(ALUA5), .pin10(ALUA4), .pin11(nAAWriteDR), .pin12(nDBReadDR), .pin13(DBRead1),
    .pin14(DBRead0), .pin15(D4), .pin16(1'b1));
  _74670 DATA2 (
    .pin1(D9), .pin2(D10), .pin3(D11), .pin4(AAWrite1), .pin5(AAWrite0), .pin6(ALUA11), .pin7(ALUA10),
    .pin8(1'b0), .pin9(ALUA9), .pin10(ALUA8), .pin11(nAAWriteDR), .pin12(nDBReadDR), .pin13(DBRead1),
    .pin14(DBRead0), .pin15(D8), .pin16(1'b1));
  _74670 DATA3 (
    .pin1(D13), .pin2(D14), .pin3(D15), .pin4(AAWrite1), .pin5(AAWrite0), .pin6(ALUA15), .pin7(ALUA14),
    .pin8(1'b0), .pin9(ALUA13), .pin10(ALUA12), .pin11(nAAWriteDR), .pin12(nDBReadDR), .pin13(DBRead1),
    .pin14(DBRead0), .pin15(D12), .pin16(1'b1));
  _74541 _30__gt__ALUA_LO__DEC (
    .pin1(not_5_out), .pin2(1'b0), .pin3(pullup_26_out), .pin4(pullup_26_out), .pin5(pullup_26_out),
    .pin6(pullup_26_out), .pin7(pullup_26_out), .pin8(pullup_26_out), .pin9(pullup_26_out), .pin10(1'b0),
    .pin11(ALUA7), .pin12(ALUA6), .pin13(ALUA5), .pin14(ALUA4), .pin15(ALUA3), .pin16(ALUA2), .pin17(ALUA1),
    .pin18(ALUA0), .pin19(nAAWriteFFxx), .pin20(1'b1));
  _74541 T8__gt__ALUA_HI (
    .pin1(nAAWrite00xx), .pin2(1'b0), .pin3(1'b0), .pin4(1'b0), .pin5(1'b0), .pin6(1'b0), .pin7(1'b0),
    .pin8(1'b0), .pin9(1'b0), .pin10(1'b0), .pin11(ALUA15), .pin12(ALUA14), .pin13(ALUA13), .pin14(ALUA12),
    .pin15(ALUA11), .pin16(ALUA10), .pin17(ALUA9), .pin18(ALUA8), .pin19(nAAWrite00xx), .pin20(1'b1));
  _74541 _00__gt__ALUA_HI (
    .pin1(nABWriteZOA), .pin2(1'b0), .pin3(1'b0), .pin4(1'b0), .pin5(1'b0), .pin6(1'b0), .pin7(1'b0),
    .pin8(1'b0), .pin9(1'b0), .pin10(1'b0), .pin11(A23), .pin12(A22), .pin13(A21), .pin14(A20), .pin15(A19),
    .pin16(A18), .pin17(A17), .pin18(A16), .pin19(nABWriterORAB), .pin20(1'b1));
  PullUp pullup_27 (.out(ALUA0));
  PullUp pullup_28 (.out(ALUA4));
  PullUp pullup_29 (.out(ALUA8));
  PullUp pullup_30 (.out(ALUA12));
  PullUp pullup_31 (.out(ALUA1));
  PullUp pullup_32 (.out(ALUA2));
  PullUp pullup_33 (.out(ALUA5));
  PullUp pullup_34 (.out(ALUA6));
  PullUp pullup_35 (.out(ALUA9));
  PullUp pullup_36 (.out(ALUA10));
  PullUp pullup_37 (.out(ALUA13));
  PullUp pullup_38 (.out(ALUA14));
  PullUp pullup_39 (.out(ALUA3));
  PullUp pullup_40 (.out(ALUA7));
  PullUp pullup_41 (.out(ALUA11));
  PullUp pullup_42 (.out(ALUA15));
  SST39SF040 CTRL0 (
    .nCE(1'b0), .nOE(1'b0), .nWE(1'b1), .VCC(1'b1), .GND(1'b0), .I_O0(_74138_2_pin1), .I_O1(_74138_2_pin2),
    .I_O2(_74138_2_pin3), .I_O3(_74138_1_pin1), .I_O4(_74138_1_pin2), .I_O5(_74138_1_pin3), .I_O6(DBRead0),
    .I_O7(DBRead1), .A0(IR1), .A1(IR2), .A2(IR3), .A3(IR4), .A4(IR5), .A5(IR6), .A6(IR7), .A7(IR8), .A8(IR9),
    .A9(IR10), .A10(IR11), .A11(IR12), .A12(IR13), .A13(IR14), .A14(IR15), .A15(seq0), .A16(seq1),
    .A17(seq2), .A18(seq3));
  SST39SF040 CTRL1 (
    .nCE(1'b0), .nOE(1'b0), .nWE(1'b1), .VCC(1'b1), .GND(1'b0), .I_O0(ABWrite0), .I_O1(ABWrite1),
    .I_O2(AB_Writer_pin14), .I_O3(AB_Writer_pin13), .I_O4(ALU_A_Writer_pin14), .I_O5(ALU_A_Writer_pin13),
    .I_O6(AAWrite0), .I_O7(AAWrite1), .A0(IR1), .A1(IR2), .A2(IR3), .A3(IR4), .A4(IR5), .A5(IR6), .A6(IR7),
    .A7(IR8), .A8(IR9), .A9(IR10), .A10(IR11), .A11(IR12), .A12(IR13), .A13(IR14), .A14(IR15), .A15(seq0),
    .A16(seq1), .A17(seq2), .A18(seq3));
  Seven_Seg_Hex seven_seg_hex_21 (.d({seq3, seq2, seq1, seq0}), .dp(1'b0));
  _74138 _74138_1 (
    .pin1(_74138_1_pin1), .pin2(_74138_1_pin2), .pin3(_74138_1_pin3), .pin4(Clock), .pin5(Clock),
    .pin6(1'b1), .pin7(nDBReadTEMP), .pin8(1'b0), .pin9(nDBReadDR), .pin10(nDBReadY), .pin11(nDBReadX),
    .pin12(nDBReadMemByte), .pin13(nDBReadMemWord), .pin14(nDBReadIR), .pin15(nDBReadPC), .pin16(1'b1));
  _74138 _74138_2 (
    .pin1(_74138_2_pin1), .pin2(_74138_2_pin2), .pin3(_74138_2_pin3), .pin4(1'b0), .pin5(1'b0), .pin6(1'b1),
    .pin7(nDBWriteNOTHING), .pin8(1'b0), .pin9(nDBWriteAB_HI), .pin10(nDBWriteAB_LO), .pin11(nDBWriteT8),
    .pin12(nDBWriteMemByte), .pin13(nDBWriteMemWord), .pin14(nDBWriteFLAGS), .pin15(nDBWriteORDB),
    .pin16(1'b1));
  _74139 ALU_A_Writer (
    .pin1(nDBReadTEMP), .pin2(DBRead0), .pin3(DBRead1), .pin4(nDBReadT8), .pin5(nDBReadT16),
    .pin6(nDBReadFLAGS), .pin7(nDBReadNOTHING), .pin8(1'b0), .pin9(nAAWriteFFxx), .pin10(nAAWriteT16),
    .pin11(nAAWrite00xx), .pin12(nAAWriteDR), .pin13(ALU_A_Writer_pin13), .pin14(ALU_A_Writer_pin14),
    .pin15(1'b0), .pin16(1'b1));
  _74139 AB_Writer (
    .pin1(nABWriterORAB), .pin2(ABWrite0), .pin3(ABWrite1), .pin4(nABWriteTOA), .pin5(nABWritePOA),
    .pin6(nABWriteLOA), .pin7(nABWriteZOA), .pin8(1'b0), .pin9(nABWriterORABY), .pin10(nABWriterORAB),
    .pin11(nABWriterXY), .pin12(nABWriterPC), .pin13(AB_Writer_pin13), .pin14(AB_Writer_pin14), .pin15(1'b0),
    .pin16(1'b1));
  LED HALT (.in(HaltCPU));
  Seven_Seg_Hex seven_seg_hex_22 (.d({1'b0, seq3, seq2, seq1}), .dp(1'b0));
  Seven_Seg_Hex seven_seg_hex_23 (.d({seq0, IR15, IR14, IR13}), .dp(1'b0));
  Seven_Seg_Hex seven_seg_hex_24 (.d({IR12, IR11, IR10, IR9}), .dp(1'b0));
  Seven_Seg_Hex seven_seg_hex_25 (.d({IR8, IR7, IR6, IR5}), .dp(1'b0));
  Seven_Seg_Hex seven_seg_hex_26 (.d({IR4, IR3, IR2, IR1}), .dp(1'b0));
  SST39SF040 ALU0 (
    .nCE(1'b0), .nOE(1'b0), .nWE(1'b1), .VCC(1'b1), .GND(1'b0), .I_O0(ALUB0), .I_O1(ALUB1), .I_O2(ALUB2),
    .I_O3(ALUB3), .I_O4(PCEnable), .I_O5(HaltCPU), .I_O6(uReset), .I_O7(ZeroFlag0), .A0(D0), .A1(D1),
    .A2(D2), .A3(D3), .A4(ALUA0), .A5(ALUA1), .A6(ALUA2), .A7(ALUA3), .A8(IR9), .A9(IR10), .A10(IR11),
    .A11(IR12), .A12(IR13), .A13(IR14), .A14(IR15), .A15(seq0), .A16(seq1), .A17(seq2), .A18(seq3));
  SST39SF040 ALU1 (
    .nCE(1'b0), .nOE(1'b0), .nWE(1'b1), .VCC(1'b1), .GND(1'b0), .I_O0(ALUB4), .I_O1(ALUB5), .I_O2(ALUB6),
    .I_O3(ALUB7), .I_O4(ORDBLoad), .I_O5(ORABLoad), .I_O6(FLAGSLoad), .I_O7(ZeroFlag1), .A0(D4), .A1(D5),
    .A2(D6), .A3(D7), .A4(ALUA4), .A5(ALUA5), .A6(ALUA6), .A7(ALUA7), .A8(IR9), .A9(IR10), .A10(IR11),
    .A11(IR12), .A12(IR13), .A13(IR14), .A14(IR15), .A15(seq0), .A16(seq1), .A17(seq2), .A18(seq3));
  SST39SF040 ALU2 (
    .nCE(1'b0), .nOE(1'b0), .nWE(1'b1), .VCC(1'b1), .GND(1'b0), .I_O0(ALUB8), .I_O1(ALUB9), .I_O2(ALUB10),
    .I_O3(ALUB11), .I_O4(ConditionEnable), .I_O5(CarryMode0), .I_O6(CarryMode1), .I_O7(ZeroFlag2), .A0(D8),
    .A1(D9), .A2(D10), .A3(D11), .A4(ALUA8), .A5(ALUA9), .A6(ALUA10), .A7(ALUA11), .A8(IR9), .A9(IR10),
    .A10(IR11), .A11(IR12), .A12(IR13), .A13(IR14), .A14(IR15), .A15(seq0), .A16(seq1), .A17(seq2), .A18(seq3));
  SST39SF040 ALU3 (
    .nCE(1'b0), .nOE(1'b0), .nWE(1'b1), .VCC(1'b1), .GND(1'b0), .I_O0(ALUB12), .I_O1(ALUB13), .I_O2(ALUB14),
    .I_O3(ALUB15), .I_O4(INTLoad), .I_O5(INTEnable), .I_O6(INTClear), .I_O7(ZeroFlag3), .A0(D12), .A1(D13),
    .A2(D14), .A3(D15), .A4(ALUA12), .A5(ALUA13), .A6(ALUA14), .A7(ALUA15), .A8(IR9), .A9(IR10), .A10(IR11),
    .A11(IR12), .A12(IR13), .A13(IR14), .A14(IR15), .A15(seq0), .A16(seq1), .A17(seq2), .A18(seq3));
  Seven_Seg_Hex seven_seg_hex_27 (.d({1'b0, seq3, seq2, seq1}), .dp(1'b0));
  Seven_Seg_Hex seven_seg_hex_28 (.d({seq0, IR15, IR14, IR13}), .dp(1'b0));
  Seven_Seg_Hex seven_seg_hex_29 (.d({IR12, IR11, IR10, IR9}), .dp(1'b0));
  Seven_Seg_Hex seven_seg_hex_30 (.d({ALUA3, ALUA2, ALUA1, ALUA0}), .dp(1'b0));
  Seven_Seg_Hex seven_seg_hex_31 (.d({D3, D2, D1, D0}), .dp(1'b0));
  Seven_Seg_Hex seven_seg_hex_32 (.d({ALUA15, ALUA14, ALUA13, ALUA12}), .dp(1'b0));
  Seven_Seg_Hex seven_seg_hex_33 (.d({ALUA11, ALUA10, ALUA9, ALUA8}), .dp(1'b0));
  _74283 ADD0 (
    .pin1(RESULT1), .pin2(ALUB1), .pin3(ALUA1), .pin4(RESULT0), .pin5(ALUA0), .pin6(ALUB0), .pin7(CarryIn),
    .pin8(1'b0), .pin9(ADD0_pin9), .pin10(RESULT3), .pin11(ALUB3), .pin12(ALUA3), .pin13(RESULT2),
    .pin14(ALUA2), .pin15(ALUB2), .pin16(1'b1));
  _74283 ADD1 (
    .pin1(RESULT5), .pin2(ALUB5), .pin3(ALUA5), .pin4(RESULT4), .pin5(ALUA4), .pin6(ALUB4), .pin7(ADD1_pin7),
    .pin8(1'b0), .pin9(ADD1_pin9), .pin10(RESULT7), .pin11(ALUB7), .pin12(ALUA7), .pin13(RESULT6),
    .pin14(ALUA6), .pin15(ALUB6), .pin16(1'b1));
  _74283 ADD2 (
    .pin1(RESULT9), .pin2(ALUB9), .pin3(ALUA9), .pin4(RESULT8), .pin5(ALUA8), .pin6(ALUB8), .pin7(ADD2_pin7),
    .pin8(1'b0), .pin9(ADD2_pin9), .pin10(RESULT11), .pin11(ALUB11), .pin12(ALUA11), .pin13(RESULT10),
    .pin14(ALUA10), .pin15(ALUB10), .pin16(1'b1));
  _74283 ADD3 (
    .pin1(RESULT13), .pin2(ALUB13), .pin3(ALUA13), .pin4(RESULT12), .pin5(ALUA12), .pin6(ALUB12),
    .pin7(ADD3_pin7), .pin8(1'b0), .pin9(CarryResult), .pin10(RESULT15), .pin11(ALUB15), .pin12(ALUA15),
    .pin13(RESULT14), .pin14(ALUA14), .pin15(ALUB14), .pin16(1'b1));
  _74153 CarryMode (
    .pin1(1'b0), .pin2(CarryMode1), .pin3(1'b0), .pin4(FlagCARRY), .pin5(1'b1), .pin6(1'b0), .pin7(CarryIn),
    .pin8(1'b0), .pin9(CarryEnable), .pin10(1'b1), .pin11(1'b1), .pin12(1'b1), .pin13(1'b0),
    .pin14(CarryMode0), .pin15(1'b0), .pin16(1'b1));
  Seven_Seg_Hex seven_seg_hex_34 (.d({ALUA7, ALUA6, ALUA5, ALUA4}), .dp(1'b0));
  Seven_Seg_Hex seven_seg_hex_35 (.d({ALUA3, ALUA2, ALUA1, ALUA0}), .dp(1'b0));
  and and_9 (ADD1_pin7, ADD0_pin9, CarryEnable);
  and and_10 (ADD2_pin7, ADD1_pin9, CarryEnable);
  and and_11 (ADD3_pin7, ADD2_pin9, CarryEnable);
  Seven_Seg_Hex seven_seg_hex_36 (.d({D15, D14, D13, D12}), .dp(1'b0));
  Seven_Seg_Hex seven_seg_hex_37 (.d({D11, D10, D9, D8}), .dp(1'b0));
  Seven_Seg_Hex seven_seg_hex_38 (.d({D7, D6, D5, D4}), .dp(1'b0));
  Seven_Seg_Hex seven_seg_hex_39 (.d({D3, D2, D1, D0}), .dp(1'b0));
  nand nand_1 (nand_1_out, nClk, FLAGSLoad, FLAGSX);
  and and_12 (and_12_out, nDBReadFLAGS, nand_2_out);
  nand nand_2 (nand_2_out, nClk, FLAGSLoad, nFLAGSX);
  nor nor_1 (FLAGSX, IR13, IR14, IR15);
  not not_6 (not_6_out, FLAGSLoad);
  and and_13 (and_13_out, ZeroFlag0, ZeroFlag1, ZeroFlag2, ZeroFlag3);
  xor xor_1 (xor_1_out, FlagCARRY, CarryMode0);
  Seven_Seg_Hex seven_seg_hex_40 (.d({ALUB15, ALUB14, ALUB13, ALUB12}), .dp(1'b0));
  xor xor_2 (xor_2_out, RESULT15, ALUA15);
  xor xor_3 (xor_3_out, RESULT15, ALUB15);
  Seven_Seg_Hex seven_seg_hex_41 (.d({ALUB11, ALUB10, ALUB9, ALUB8}), .dp(1'b0));
  nand nand_3 (nand_3_out, ORDBLoad, nClk);
  _74574 OR_DB_LOW (
    .pin1(nDBWriteORDB), .pin2(RESULT0), .pin3(RESULT1), .pin4(RESULT2), .pin5(RESULT3), .pin6(RESULT4),
    .pin7(RESULT5), .pin8(RESULT6), .pin9(RESULT7), .pin10(1'b0), .pin11(nand_3_out), .pin12(D7), .pin13(D6),
    .pin14(D5), .pin15(D4), .pin16(D3), .pin17(D2), .pin18(D1), .pin19(D0), .pin20(1'b1));
  _74574 OR_DB_HI (
    .pin1(nDBWriteORDB), .pin2(RESULT8), .pin3(RESULT9), .pin4(RESULT10), .pin5(RESULT11), .pin6(RESULT12),
    .pin7(RESULT13), .pin8(RESULT14), .pin9(RESULT15), .pin10(1'b0), .pin11(nand_3_out), .pin12(D15),
    .pin13(D14), .pin14(D13), .pin15(D12), .pin16(D11), .pin17(D10), .pin18(D9), .pin19(D8), .pin20(1'b1));
  nand nand_4 (nand_4_out, CarryMode1, FLAGSX, xor_1_out);
  Seven_Seg_Hex seven_seg_hex_42 (.d({ALUB7, ALUB6, ALUB5, ALUB4}), .dp(1'b0));
  _74173 SR__IR_00_03 (
    .pin1(nFLAGSX), .pin2(nFLAGSX), .pin3(FlagCARRY), .pin4(FlagZERO), .pin5(FlagNEG), .pin6(FlagOVERFLOW),
    .pin7(nand_1_out), .pin8(1'b0), .pin9(1'b0), .pin10(1'b0), .pin11(F3), .pin12(F2), .pin13(F1),
    .pin14(F0), .pin15(1'b0), .pin16(1'b1));
  _74173 SR__IR_04_1F (
    .pin1(FLAGSX), .pin2(FLAGSX), .pin3(FlagCARRY), .pin4(FlagZERO), .pin5(FlagNEG), .pin6(FlagOVERFLOW),
    .pin7(and_12_out), .pin8(1'b0), .pin9(1'b0), .pin10(1'b0), .pin11(F3), .pin12(F2), .pin13(F1),
    .pin14(F0), .pin15(1'b0), .pin16(1'b1));
  _74257 FLAGS_MUX (
    .pin1(not_6_out), .pin2(CarryResult), .pin3(D0), .pin4(F0), .pin5(and_13_out), .pin6(D1), .pin7(F1),
    .pin8(1'b0), .pin9(F2), .pin10(D2), .pin11(RESULT15), .pin12(F3), .pin13(D3), .pin14(FLAGS_MUX_pin14),
    .pin15(1'b0), .pin16(1'b1));
  and and_14 (FLAGS_MUX_pin14, xor_2_out, xor_3_out);
  Seven_Seg_Hex seven_seg_hex_43 (.d({ALUB3, ALUB2, ALUB1, ALUB0}), .dp(1'b0));
  nand nand_5 (nuReset, nand_4_out, uReset);
  not not_7 (nFLAGSX, FLAGSX);
  Seven_Seg_Hex seven_seg_hex_44 (.d({RESULT15, RESULT14, RESULT13, RESULT12}), .dp(1'b0));
  Seven_Seg_Hex seven_seg_hex_45 (.d({RESULT11, RESULT10, RESULT9, RESULT8}), .dp(1'b0));
  Seven_Seg_Hex seven_seg_hex_46 (.d({RESULT7, RESULT6, RESULT5, RESULT4}), .dp(1'b0));
  Seven_Seg_Hex seven_seg_hex_47 (.d({RESULT3, RESULT2, RESULT1, RESULT0}), .dp(1'b0));
  and and_15 (and_15_out, nABWriterORABY, nABWriterORAB);
  xor xor_4 (xor_4_out, FlagOVERFLOW, FlagNEG);
  nand nand_6 (nand_6_out, INTLoad, nClk);
  not not_8 (nFlagCARRY, FlagCARRY);
  not not_9 (not_9_out, FlagZERO);
  not not_10 (not_10_out, ConditionEnable);
  not not_11 (not_11_out, nIRQ);
  nand nand_7 (nand_7_out, ORABLoad, nClk);
  _74574 OR_AB_LOW (
    .pin1(and_15_out), .pin2(RESULT0), .pin3(RESULT1), .pin4(RESULT2), .pin5(RESULT3), .pin6(RESULT4),
    .pin7(RESULT5), .pin8(RESULT6), .pin9(RESULT7), .pin10(1'b0), .pin11(nand_7_out), .pin12(A7), .pin13(A6),
    .pin14(A5), .pin15(A4), .pin16(A3), .pin17(A2), .pin18(A1), .pin19(A0), .pin20(1'b1));
  _74574 OR_AB_HI (
    .pin1(and_15_out), .pin2(RESULT8), .pin3(RESULT9), .pin4(RESULT10), .pin5(RESULT11), .pin6(RESULT12),
    .pin7(RESULT13), .pin8(RESULT14), .pin9(RESULT15), .pin10(1'b0), .pin11(nand_7_out), .pin12(A15),
    .pin13(A14), .pin14(A13), .pin15(A12), .pin16(A11), .pin17(A10), .pin18(A9), .pin19(A8), .pin20(1'b1));
  not not_12 (not_12_out, xor_4_out);
  _74541 STATUS_Buffer (
    .pin1(nDBWriteFLAGS), .pin2(FlagCARRY), .pin3(FlagZERO), .pin4(FlagNEG), .pin5(FlagOVERFLOW),
    .pin6(INT0), .pin7(INT1), .pin8(INT2), .pin9(INTEnabled), .pin10(1'b0), .pin11(D7), .pin12(D6),
    .pin13(D5), .pin14(D4), .pin15(D3), .pin16(D2), .pin17(D1), .pin18(D0), .pin19(nDBWriteFLAGS),
    .pin20(1'b1));
  or or_3 (or_3_out, FlagZERO, xor_4_out);
  and and_16 (and_16_out, not_12_out, not_9_out);
  _74151 FLAGS_Selector (
    .pin1(nFlagCARRY), .pin2(FlagCARRY), .pin3(not_9_out), .pin4(FlagZERO), .pin5(ConditionResult),
    .pin7(not_10_out), .pin8(1'b0), .pin9(IR7), .pin10(IR6), .pin11(IR5), .pin12(or_3_out),
    .pin13(not_12_out), .pin14(and_16_out), .pin15(xor_4_out), .pin16(1'b1));  // open: pin6
  and and_17 (and_17_out, ConditionResult, ConditionEnable);
  _7474 INT_Enable_Disable (
    .pin1(nReset), .pin2(INTEnable), .pin3(nand_6_out), .pin4(1'b1), .pin5(INTEnabled), .pin6(nINTEnabled),
    .pin7(1'b0), .pin10(1'b1), .pin11(1'b1), .pin12(1'b1), .pin13(1'b1), .pin14(1'b1));  // open: pin8, pin9
  and and_18 (INTCondition, INTEnabled, nINT_Ack, not_11_out);
  LED Zero (.in(FlagZERO));
  LED Carry (.in(FlagCARRY));
  LED Negative (.in(FlagNEG));
  LED MemoryAccess (.in(MemAccess));
  LED INT_Enabled (.in(INTEnabled));
  not not_13 (not_13_out, and_17_out);
  or or_4 (nBranchTaken, IR8, not_13_out);
  and and_19 (SccTrue, and_17_out, IR8);
  and and_20 (and_20_out, nDBWriteMemWord, nDBReadMemWord);
  and and_21 (and_21_out, nDBReadMemWord, nDBReadMemByte);
  and and_22 (R_nW, nDBWriteMemWord, nDBWriteMemByte);
  and and_23 (nDBRWMemByte, nDBReadMemByte, nDBWriteMemByte);
  and and_24 (and_24_out, nReset, nuReset);
  not not_14 (not_14_out, nDBReadIR);
  not not_15 (not_15_out, INTClear);
  _74245 LowLow (
    .pin1(R_nW), .pin2(D0), .pin3(D1), .pin4(D2), .pin5(D3), .pin6(D4), .pin7(D5), .pin8(D6), .pin9(D7),
    .pin10(1'b0), .pin11(DB7), .pin12(DB6), .pin13(DB5), .pin14(DB4), .pin15(DB3), .pin16(DB2), .pin17(DB1),
    .pin18(DB0), .pin19(nOELowLow), .pin20(1'b1));
  _74245 HighLow (
    .pin1(R_nW), .pin2(D0), .pin3(D1), .pin4(D2), .pin5(D3), .pin6(D4), .pin7(D5), .pin8(D6), .pin9(D7),
    .pin10(1'b0), .pin11(DB15), .pin12(DB14), .pin13(DB13), .pin14(DB12), .pin15(DB11), .pin16(DB10),
    .pin17(DB9), .pin18(DB8), .pin19(nOEHighLow), .pin20(1'b1));
  _74245 HighHigh (
    .pin1(R_nW), .pin2(D8), .pin3(D9), .pin4(D10), .pin5(D11), .pin6(D12), .pin7(D13), .pin8(D14),
    .pin9(D15), .pin10(1'b0), .pin11(DB15), .pin12(DB14), .pin13(DB13), .pin14(DB12), .pin15(DB11),
    .pin16(DB10), .pin17(DB9), .pin18(DB8), .pin19(nOEHighHigh), .pin20(1'b1));
  and and_25 (and_25_out, and_21_out, R_nW);
  _7474 INT_Ack__IR_Disable (
    .pin1(and_24_out), .pin2(INTCondition), .pin3(not_14_out), .pin4(1'b1), .pin5(IR_Disable),
    .pin6(nIR_Disable), .pin7(1'b0), .pin8(nINT_Ack), .pin9(INT_Ack), .pin10(1'b1), .pin11(IR_Disable),
    .pin12(1'b1), .pin13(INT_Ack__IR_Disable_pin13), .pin14(1'b1));
  and and_26 (INT_Ack__IR_Disable_pin13, not_15_out, nReset);
  _74148 INT_Priority (
    .pin1(nIRQ4), .pin2(nIRQ5), .pin3(nIRQ6), .pin4(INT_Timer_6Hz), .pin5(1'b0), .pin6(INT2), .pin7(INT1),
    .pin8(1'b0), .pin9(INT0), .pin10(nIRQ0), .pin11(nIRQ1), .pin12(nIRQ2), .pin13(nIRQ3), .pin14(nIRQ),
    .pin16(1'b1));  // open: pin15
  not not_16 (MemAccess, and_25_out);
  not not_17 (not_17_out, A0);
  and and_27 (and_27_out, MemAccess, A0);
  or or_5 (or_5_out, not_17_out, nDBRWMemByte);
  PullUp pullup_43 (.out(nIRQ0));
  PullUp pullup_44 (.out(nIRQ1));
  PullUp pullup_45 (.out(nIRQ4));
  PullUp pullup_46 (.out(nIRQ5));
  PullUp pullup_47 (.out(nIRQ3));
  PullUp pullup_48 (.out(nIRQ2));
  PullUp pullup_49 (.out(nIRQ6));
  PullUp pullup_50 (.out(INT_Timer_6Hz));
  or or_6 (nOEHighHigh, and_20_out, and_25_out);
  or or_7 (nOELowLow, and_25_out, and_27_out);
  or or_8 (nOEHighLow, and_25_out, or_5_out);
  not not_18 (not_18_out, A0);
  SST39SF040 ROM0_PROGRAM_LO (
    .nCE(nROM_F0_CS), .nOE(nOE_LOW), .nWE(1'b1), .VCC(1'b1), .GND(1'b0), .I_O0(DB0), .I_O1(DB1), .I_O2(DB2),
    .I_O3(DB3), .I_O4(DB4), .I_O5(DB5), .I_O6(DB6), .I_O7(DB7), .A0(A1), .A1(A2), .A2(A3), .A3(A4), .A4(A5),
    .A5(A6), .A6(A7), .A7(A8), .A8(A9), .A9(A10), .A10(A11), .A11(A12), .A12(A13), .A13(A14), .A14(A15),
    .A15(A16), .A16(A17), .A17(A18), .A18(A19));
  SST39SF040 ROM1_LOOKUP_LO (
    .nCE(nROM_E0_CS), .nOE(nOE_LOW), .nWE(1'b1), .VCC(1'b1), .GND(1'b0), .I_O0(DB0), .I_O1(DB1), .I_O2(DB2),
    .I_O3(DB3), .I_O4(DB4), .I_O5(DB5), .I_O6(DB6), .I_O7(DB7), .A0(A1), .A1(A2), .A2(A3), .A3(A4), .A4(A5),
    .A5(A6), .A6(A7), .A7(A8), .A8(A9), .A9(A10), .A10(A11), .A11(A12), .A12(A13), .A13(A14), .A14(A15),
    .A15(A16), .A16(A17), .A17(A18), .A18(A19));
  AS6C4008 RAM0_LO (
    .A0(A1), .A1(A2), .A2(A3), .A3(A4), .A4(A5), .A5(A6), .A6(A7), .A7(A8), .A8(A9), .A9(A10), .A10(A11),
    .A11(A12), .A12(A13), .nCE(nRAM_00_CS), .nOE(nOE_LOW), .nWE(nWE_LOW), .DQ0(DB0), .DQ1(DB1), .DQ2(DB2),
    .DQ3(DB3), .DQ4(DB4), .DQ5(DB5), .DQ6(DB6), .DQ7(DB7), .VCC(1'b1), .GND(1'b0), .A13(A14), .A14(A15),
    .A15(A16), .A16(A17), .A17(A18), .A18(A19));
  AS6C4008 RAM1_LO (
    .A0(A1), .A1(A2), .A2(A3), .A3(A4), .A4(A5), .A5(A6), .A6(A7), .A7(A8), .A8(A9), .A9(A10), .A10(A11),
    .A11(A12), .A12(A13), .nCE(nRAM_10_CS), .nOE(nOE_LOW), .nWE(nWE_LOW), .DQ0(DB0), .DQ1(DB1), .DQ2(DB2),
    .DQ3(DB3), .DQ4(DB4), .DQ5(DB5), .DQ6(DB6), .DQ7(DB7), .VCC(1'b1), .GND(1'b0), .A13(A14), .A14(A15),
    .A15(A16), .A16(A17), .A17(A18), .A18(A19));
  or or_9 (or_9_out, nDBReadMemByte, not_18_out);
  or or_10 (or_10_out, nDBReadMemByte, A0);
  or or_11 (or_11_out, not_18_out, nDBWriteMemByte);
  or or_12 (or_12_out, A0, nDBWriteMemByte);
  and and_28 (nWE_HIGH, nDBReadMemWord, or_9_out);
  and and_29 (nWE_LOW, nDBReadMemWord, or_10_out);
  and and_30 (nOE_HIGH, or_11_out, nDBWriteMemWord);
  and and_31 (nOE_LOW, or_12_out, nDBWriteMemWord);
  SST39SF040 ROM0_PROGRAM_HI (
    .nCE(nROM_F0_CS), .nOE(nOE_HIGH), .nWE(1'b1), .VCC(1'b1), .GND(1'b0), .I_O0(DB8), .I_O1(DB9),
    .I_O2(DB10), .I_O3(DB11), .I_O4(DB12), .I_O5(DB13), .I_O6(DB14), .I_O7(DB15), .A0(A1), .A1(A2), .A2(A3),
    .A3(A4), .A4(A5), .A5(A6), .A6(A7), .A7(A8), .A8(A9), .A9(A10), .A10(A11), .A11(A12), .A12(A13),
    .A13(A14), .A14(A15), .A15(A16), .A16(A17), .A17(A18), .A18(A19));
  SST39SF040 ROM1_LOOKUP_HI (
    .nCE(nROM_E0_CS), .nOE(nOE_HIGH), .nWE(1'b1), .VCC(1'b1), .GND(1'b0), .I_O0(DB8), .I_O1(DB9),
    .I_O2(DB10), .I_O3(DB11), .I_O4(DB12), .I_O5(DB13), .I_O6(DB14), .I_O7(DB15), .A0(A1), .A1(A2), .A2(A3),
    .A3(A4), .A4(A5), .A5(A6), .A6(A7), .A7(A8), .A8(A9), .A9(A10), .A10(A11), .A11(A12), .A12(A13),
    .A13(A14), .A14(A15), .A15(A16), .A16(A17), .A17(A18), .A18(A19));
  AS6C4008 RAM0_HI (
    .A0(A1), .A1(A2), .A2(A3), .A3(A4), .A4(A5), .A5(A6), .A6(A7), .A7(A8), .A8(A9), .A9(A10), .A10(A11),
    .A11(A12), .A12(A13), .nCE(nRAM_00_CS), .nOE(nOE_HIGH), .nWE(nWE_HIGH), .DQ0(DB8), .DQ1(DB9), .DQ2(DB10),
    .DQ3(DB11), .DQ4(DB12), .DQ5(DB13), .DQ6(DB14), .DQ7(DB15), .VCC(1'b1), .GND(1'b0), .A13(A14), .A14(A15),
    .A15(A16), .A16(A17), .A17(A18), .A18(A19));
  AS6C4008 RAM1_HI (
    .A0(A1), .A1(A2), .A2(A3), .A3(A4), .A4(A5), .A5(A6), .A6(A7), .A7(A8), .A8(A9), .A9(A10), .A10(A11),
    .A11(A12), .A12(A13), .nCE(nRAM_10_CS), .nOE(nOE_HIGH), .nWE(nWE_HIGH), .DQ0(DB8), .DQ1(DB9), .DQ2(DB10),
    .DQ3(DB11), .DQ4(DB12), .DQ5(DB13), .DQ6(DB14), .DQ7(DB15), .VCC(1'b1), .GND(1'b0), .A13(A14), .A14(A15),
    .A15(A16), .A16(A17), .A17(A18), .A18(A19));
  _74138 Decoder_00_07__1MB (
    .pin1(A20), .pin2(A21), .pin3(A22), .pin4(A23), .pin5(1'b0), .pin6(1'b1), .pin7(nMEM_70), .pin8(1'b0),
    .pin9(nMEM_60), .pin10(nMEM_50), .pin11(nMEM_40), .pin12(nMEM_30), .pin13(nMEM_20), .pin14(nRAM_10_CS),
    .pin15(nRAM_00_CS), .pin16(1'b1));
  _74138 Decoder_08_0F__1MB (
    .pin1(A20), .pin2(A21), .pin3(A22), .pin4(1'b0), .pin5(1'b0), .pin6(A23), .pin7(nROM_F0_CS), .pin8(1'b0),
    .pin9(nROM_E0_CS), .pin10(nMEM_D0), .pin11(nMEM_C0), .pin12(nMEM_B0), .pin13(nMEM_A0), .pin14(nMEM_90),
    .pin15(nMEM_80), .pin16(1'b1));
  _74138 I_O__D8xxxx__512KB (
    .pin1(A16), .pin2(A17), .pin3(A18), .pin4(nMEM_D0), .pin5(nMEM_D0), .pin6(A19), .pin7(nMEM_DF0000),
    .pin8(1'b0), .pin9(nMEM_DE0000), .pin10(nMEM_DD0000), .pin11(nMEM_DC0000), .pin12(nMEM_DB0000),
    .pin13(nMEM_DA0000), .pin14(nMEM_D90000), .pin15(nMEM_D80000), .pin16(1'b1));
  nor nor_2 (nor_2_out, nMEM_DF0000, nWE_LOW);
  nor nor_3 (nor_3_out, nMEM_DE0000, nClk);
  or or_13 (or_13_out, nOE_HIGH, nMEM_DE0000, nOE_LOW);
  Terminal #(.termWidth(80)) Terminal (.D({DB7, DB6, DB5, DB4, DB3, DB2, DB1, DB0}), .C(Clock), .en(nor_2_out));
  not not_19 (not_19_out, or_13_out);
  _74541 _74541_1 (
    .pin1(or_13_out), .pin2(_74541_1_pin2[0]), .pin3(_74541_1_pin2[1]), .pin4(_74541_1_pin2[2]),
    .pin5(_74541_1_pin2[3]), .pin6(_74541_1_pin2[4]), .pin7(_74541_1_pin2[5]), .pin8(_74541_1_pin2[6]),
    .pin9(_74541_1_pin2[7]), .pin10(1'b0), .pin11(DB7), .pin12(DB6), .pin13(DB5), .pin14(DB4), .pin15(DB3),
    .pin16(DB2), .pin17(DB1), .pin18(DB0), .pin19(or_13_out), .pin20(1'b1));
  _74541 _74541_2 (
    .pin1(or_13_out), .pin2(_74541_1_pin2[8]), .pin3(_74541_1_pin2[9]), .pin4(_74541_1_pin2[10]),
    .pin5(_74541_1_pin2[11]), .pin6(_74541_1_pin2[12]), .pin7(_74541_1_pin2[13]), .pin8(_74541_1_pin2[14]),
    .pin9(_74541_1_pin2[15]), .pin10(1'b0), .pin11(DB15), .pin12(DB14), .pin13(DB13), .pin14(DB12),
    .pin15(DB11), .pin16(DB10), .pin17(DB9), .pin18(DB8), .pin19(or_13_out), .pin20(1'b1));
  Keyboard keyboard_1 (.C(nor_3_out), .en(not_19_out), .D(_74541_1_pin2));  // open: av

  assign nIRQ7 = INT_Timer_6Hz;

  // Other names for the same wires on the sheet: Clk = Clock; SR0 = FlagCARRY; SR1 = FlagZERO; SR2 = FlagNEG;
  //   SR3 = FlagOVERFLOW

  // Notes on the sheet:
  //   Clock: Hz: 2147483647
  //   INT_Timer_6Hz: Hz: 6
  //   Allows PC-LO to be
  //   loaded on it's own
  //   If DBReadPC and DBRead0 
  //   are LOW then PC-HI gets 
  //   loaded with T8
  //   PROGRAM COUNTER (PC)
  //   PROGRAM COUNTER
  //   ADDRESS BUS
  //   PC to AB
  //   AB to DB
  //   X & Y INDEX REGISTERS
  //   Write X (DB Reader)
  //   Read X and Y (AB Writer)
  //   T16 REGISTER (T16)
  //   DATA BUS
  //   T8 REGISTER (T8)
  //   00 T8-5 to ALU-A
  //   T8 to DB-LO
  //   T8 to AB-HI
  //   INSTRUCTION REGISTER (IR)
  //   0000 or 0002 to ALU-A (INC)
  //   INSTRUCTION REG
  //   Microcode Sequencer
  //   T8 to AB-HI (Lookup)
  //   $00 to DB-HI
  //   DATA REGISTERS (DR)
  //   DR Write (DBReaderDR)
  //   DR Read (AAWriterDR)
  //   FFFF to ALU-A (DEC)
  //   $00 to ALUA-HI
  //   $00 to AB-HI
  //   MC STEP
  //   CONTROL
  //   CTRL0 ADDRESS
  //   ALU
  //   ALU-0 ADDRESS
  //   ALU-A (AA Bus)
  //   ADDERS
  //   CARRY MODE
  //   ALU-B (Data Bus)
  //   STATUS REGISTERS (SR)
  //   ALU-B (ROM Output)
  //   CARRY SKIP
  //   OUTPUT REGISTERS
  //   ORDB
  //   ALU RESULT (AA + ROM)
  //   STATUS BUFFER
  //   INTERRUPT ENABLE
  //   OUTPUT REGISTER
  //   ORAB
  //   INT-ACK  INT-DISABLE
  //   INTERRUPT PRIORITY
  //   MEMORY BUFFERS
  //   Byte/Word Addressing
  //   K16 CPU
  //   EXTERNAL MEMORY
  //   (seperate board)
  //   contents of CTRL1 (hex, n*v repeats v):
  //   CONTROL1.hex false
  //   contents of CTRL0 (hex, n*v repeats v):
  //   CONTROL0.hex false
  //   contents of ROM1-LOOKUP-LO (hex, n*v repeats v):
  //   LOOKUP_LO.hex false
  //   contents of ALU2 (hex, n*v repeats v):
  //   ALU2.hex false
  //   contents of ROM0-PROGRAM-LO (hex, n*v repeats v):
  //   ProgramLOW.hex false
  //   contents of ALU3 (hex, n*v repeats v):
  //   ALU3.hex false
  //   contents of ROM1-LOOKUP-HI (hex, n*v repeats v):
  //   LOOKUP_HI.hex false
  //   contents of ALU0 (hex, n*v repeats v):
  //   ALU0.hex false
  //   contents of ROM0-PROGRAM-HI (hex, n*v repeats v):
  //   ProgramHIGH.hex false
  //   contents of ALU1 (hex, n*v repeats v):
  //   ALU1.hex false
endmodule
